// Logisim project 5.circ as structural Verilog: 1 circuit, main circuit main
module main (
);

  wire Control_p2, Control_p3, Control_p4, Control_p5, undriven_3;
  wire [1:0] Control_p6, INSTRUCTION_MEMORY_PC_p1, INSTRUCTION_MEMORY_PC_p3, INSTRUCTION_MEMORY_PC_p5,
       INSTRUCTION_MEMORY_PC_p7;
  wire [3:0] ALU_output, undriven, undriven_2;

  // Q4B3_main INSTRUCTION_MEMORY_PC: pin names not known; wires that end beside it: INSTRUCTION_MEMORY_PC_p1[0], INSTRUCTION_MEMORY_PC_p1[1], INSTRUCTION_MEMORY_PC_p3[0], INSTRUCTION_MEMORY_PC_p3[1], INSTRUCTION_MEMORY_PC_p5[0], INSTRUCTION_MEMORY_PC_p5[1], INSTRUCTION_MEMORY_PC_p7[0], INSTRUCTION_MEMORY_PC_p7[1]
  Multiplexer #(.width(2), .enable("false")) multiplexer_1 (
    .in0(INSTRUCTION_MEMORY_PC_p5), .in1(INSTRUCTION_MEMORY_PC_p7), .sel(Control_p2));  // open: out
  Multiplexer #(.width(4), .enable("false")) multiplexer_2 (
    .in0(ALU_output), .in1(undriven), .sel(Control_p3));  // open: out
  // ControlTruth Control: pin names not known; wires that end beside it: INSTRUCTION_MEMORY_PC_p1, Control_p2, Control_p3, Control_p4, Control_p5, Control_p6
  ALU ALU (.Input2(undriven_2), .ControlBits(Control_p6), .Output(ALU_output));  // open: Input1, CarryOut, Zero
  Diarmuid_Ryan_11363776_A4_main DATA_MEM_REG (
    .RegWrite_2(Control_p4), .MemAdd(ALU_output), .MemWrite(undriven_3), .ExtDataWrite(Control_p5),
    .ExtData(undriven));  // open: RegRead1, RegRead2, RegWrite, CLK

  // Notes on the sheet:
  //   OP
  //   RS
  //   RT
  //   RD/Offset
endmodule
